# Fritzing sketch clock (saved by Fritzing 0.9.4)
circuit board: 8.46667cm x 5.64444cm
breadboards: 2

parts:
  Part1 = Arduino Nano (Rev3.0)
  U1 = 555 Timer [package="DIP8 [THT]"]
  R1 = Resistor [tolerance=±5% resistance=1k package=THT]
  R3 = Resistor [tolerance=±5% resistance=220 package=THT]
  LED1 = smd LED [color="Yellow (595nm)" package="1206 [SMD]"]
  C1 = Electrolytic Capacitor [capacitance=1µF package="100 mil [THT, electrolytic]"]
  C2 = Tantalum Capacitor [capacitance="1 μF" package="B 3528 [SMD, tantalum]"]
  C3 = Tantalum Capacitor [capacitance="1 μF" package="B 3528 [SMD, tantalum]"]
  R4 = Rotary Potentiometer (Large) [maximum_resistance=100kΩ package=THT]
  R5 = Resistor [tolerance=±5% resistance=1k package=THT]

nets:
  N1: Part1.GND, U1.Ground, R3.Pin_0, C2.-, C3.-
  N2: Part1.5V, U1.Reset, U1.Vcc_Supply_Voltage, R1.Pin_0, C3.+
  N3: U1.Trigger, U1.Threshold, C1.+, R4.wiper
  N4: U1.Output, LED1.anode
  N5: U1.Control_Voltage, C2.+
  N6: U1.Discharge, R1.Pin_1, R5.Pin_1
  N7: R3.Pin_1, LED1.cathode
  N8: R4.leg2, R5.Pin_0
